# Fritzing sketch TV-B-Gone Shield (saved by Fritzing 0.7.0b)
stripboards: 1
perfboards: 1

parts:
  S3 = Pushbutton [package="[THT]"]
  LED1 = LED - 3mm [color="Infrared (940nm)" package="3 mm [THT]"]
  R1 = Resistor [tolerance=±5% resistance=10 package=THT]
  R2 = Resistor [tolerance=±5% resistance=47 package=THT]
  Q1 = NPN-Transistor [package="TO92 [THT]"]
  R3 = Resistor [tolerance=±5% resistance=10k package=THT]
  5V = female pin header, 6 pins [form="♀ (female)"]
  GND = female pin header, 6 pins [form="♀ (female)"]

nets:
  N1: S3.Pin_1, S3.Pin_2, Q1.E, R3.Pin_0, GND.pin3
  N2: S3.Pin_3, S3.Pin_4, 5V.pin2
  N3: LED1.cathode, Q1.C
  N4: LED1.anode, R1.Pin_0
  N5: R1.Pin_1, 5V.pin5
  N6: R2.Pin_0, Q1.B
  N7: R2.Pin_1, 5V.pin1
  N8: R3.Pin_1, GND.pin1

notes:
  seen from above
  from under
